# Fritzing sketch AnalogTemperatureSensor (saved by Fritzing 0.8.7b)
circuit board: 3.59177cm x 2.77595cm
breadboards: 1

parts:
  T1 = LM35 Temperature Sensor [package="TO92 [THT]"]
  REF03 = IC, DIP package, 8 pins [chip_label=IC]
  C2 = Tantalum Capacitor [capacitance=10µF voltage=35V package="100 mil [THT, tantalum]"]
  R1 = Resistor [tolerance=±5% resistance=220 package=THT]
  MCP601 = IC, DIP package, 8 pins [chip_label=IC]
  MCP3204 = IC, DIP package, 14 pins [chip_label=IC]
  C3 = Ceramic Capacitor [capacitance=100nF package="100 mil [THT, multilayer]"]
  C4 = Ceramic Capacitor [capacitance=100nF voltage=35V package="100 mil [THT, multilayer]"]
  C5 = Ceramic Capacitor [capacitance=100nF package="100 mil [THT, multilayer]"]
  J1 = male pin header, 7 pins [form="♂ (male)"]
  C6 = Ceramic Capacitor [capacitance=100nF package="100 mil [THT, multilayer]"]
  C7 = Ceramic Capacitor [capacitance=100nF package="100 mil [THT, multilayer]"]

nets:
  +3V3/3.3V: T1.+Vs, MCP601.pin7, MCP3204.pin14, C3.1, J1.pin2, C6.1, C7.1
  N1: T1.Vout, R1.Pin_1
  GND: T1.GND, REF03.pin4, C2.-, MCP601.pin4, MCP3204.pin7, MCP3204.pin12, C4.0, C5.0, J1.pin7, C6.0, C7.0
  +5V/5V: REF03.pin2, C2.+, C5.1, J1.pin1
  VREF: REF03.pin6, MCP3204.pin13
  T_OUT: R1.Pin_0, MCP601.pin3, C4.1
  OP_OUT: MCP601.pin2, MCP601.pin6, MCP3204.pin1
  /CS: MCP3204.pin8, J1.pin3
  DIN: MCP3204.pin9, J1.pin5
  DOUT: MCP3204.pin10, J1.pin6
  CLK: MCP3204.pin11, J1.pin4

notes:
  GND
  DO
  DIN
  CLK
  /CS
  +3V3
  +5V
  Analog Tempearture Sensor
